# Fritzing sketch robot_scetch (saved by Fritzing 0.8.7b)
breadboards: 1

parts:
  Driver1 = 28BYJ-48 Driver Module [part_number=ULN2003 package=THT]
  Bauteil2 = Arduino Nano (Rev3.0)
  Driver3 = 28BYJ-48 Driver Module [part_number=ULN2003 package=THT]
  BAT1 = BC9VPC [package=bc9vpc]
  SM1 = 28BYJ-48 Stepper Motor [part_number=28BYJ-48]  # not connected
  SM2 = 28BYJ-48 Stepper Motor [part_number=28BYJ-48]

nets:
  N1: Driver1.IN1, Bauteil2.D6
  N2: Driver1.IN2, Bauteil2.D7
  N3: Driver1.IN3, Bauteil2.D8
  N4: Driver1.IN4, Bauteil2.D9
  GND: Driver1.GND, Bauteil2.GND, Driver3.GND, BAT1.V-
  N5: Driver1.Vmotor, Driver3.Vmotor, BAT1.V+
  N6: Driver1.blue-pin, SM2.blue-pin
  N7: Driver1.pink-pin, SM2.pink-pin
  N8: Driver1.yellow-pin, SM2.yellow-pin
  N9: Driver1.orange-pin, SM2.orange-pin
  N10: Driver1.red-pin, SM2.red-pin
  N11: Bauteil2.D2, Driver3.IN1
  N12: Bauteil2.D3, Driver3.IN2
  N13: Bauteil2.D4, Driver3.IN3
  N14: Bauteil2.D5, Driver3.IN4

custom parts:
  28BYJ-48 Driver Module: High-power ULN2003 Stepper Motor Driver Board Test Module For Arduino AVR SMD
  28BYJ-48 Stepper Motor: Unipolar Stepper Motor 28BYJ-48 Top coil - pink & orange Bottom coil - blue & yellow Common rail - red Connector pins: blue - pink - yellow - orange - red
